# Fritzing sketch Esp32 (saved by Fritzing 0.9.9b)

parts:
  ESP32_-_Back1 = ESP32 - CAM
  J1 = micro USB connector MK5P [package=usb-microb]

nets:
  GND: ESP32_-_Back1.GND, J1.GND
  5V: ESP32_-_Back1.5V, J1.VCC

custom parts:
  ESP32 - CAM: The ESP32-CAM has a very competitive small-size camera module that can operate independently as a minimum system with a footprint of only 27*40.5*4.5mm and a deep sleep current of up to 6mA.
  micro USB connector MK5P: micro USB connector which only uses holes no slots. Apparently a standard of some kind called MK5P. Note the text in pcb that marks the edge of the board (and the amount the connector protudes) will both be truncated from the final board if aligned correctly.
